# Fritzing sketch DS3231nano (saved by Fritzing 0.9.2b)

parts:
  元件1 = Adafruit DS3231 [part_number="Adafruit #3013"]
  元件2 = Arduino Nano (Rev3.0) (ICSP)

nets:
  VIN: 元件1.Vin, 元件2.5V
  GND: 元件1.GND, 元件2.GND
  N1: 元件1.SCL, 元件2.A5
  N2: 元件1.SDA, 元件2.A4

custom parts:
  Adafruit DS3231: The datasheet for the DS3231 explains that this part is an "Extremely Accurate I²C-Integrated RTC/TCXO/Crystal". And, hey, it does exactly what it says on the tin! This Real Time Clock (RTC) is the most precise you can get in a small, low power package. Most RTCs use an external 32kHz timing crystal that is used to keep time with low current draw. And that's all well and good, but those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
