# Fritzing sketch opendoor (saved by Fritzing 0.9.4)

parts:
  元件1 = Arduino Nano (Rev3.0)
  IR_Recevier_VS1838 = IR Receiver Breakout [package=PCB]
  DS3231 = ZS-042 RTC Module
  LED2 = 7-SEGMENT-4DIGIT-YOUNGSUN [package=7-segment-4digit-youngsun-longpads]  # not connected
  MAX7219 = 7-SEGMENT-4DIGIT-YOUNGSUN [package=7-segment-4digit-youngsun-longpads]  # not connected
  VCC = Header 1 [package=smtra-256-8-6]  # not connected
  GND = Header 1 [package=smtra-256-8-6]
  DIN = Header 1 [package=smtra-256-8-6]
  CS = Header 1 [package=smtra-256-8-6]
  CLK = Header 1 [package=smtra-256-8-6]
  繼電器低電位觸發 = songle relay
  遙控器按鍵接點 = LilyPad Button Board

nets:
  GND: 元件1.GND, IR_Recevier_VS1838.GND, DS3231.GND, GND.1
  N1: 元件1.D7, IR_Recevier_VS1838.OUT
  N2: 元件1.D8, 繼電器低電位觸發.COMMON
  N3: 元件1.D10, DIN.1
  N4: 元件1.D11/MOSI, CS.1
  N5: 元件1.D12/MISO, CLK.1
  VCC: 元件1.5V, IR_Recevier_VS1838.VCC, DS3231.VCC
  N6: 元件1.A5, DS3231.SCL
  N7: 元件1.A4, DS3231.SDA
  N8: 繼電器低電位觸發.NO, 遙控器按鍵接點.-
  N9: 繼電器低電位觸發.NC, 遙控器按鍵接點.S
